# Fritzing sketch rPiezos_sketch (saved by Fritzing 0.9.3b)
breadboards: 1

parts:
  TRS1 = Audio Jack (TRS) 3.5mm [package="PG203J [THT]"]
  D1 = Rectifier Diode
  TRS2 = Audio Jack (TRS) 3.5mm [package="PG203J [THT]"]
  TRS3 = Audio Jack (TRS) 3.5mm [package="PG203J [THT]"]
  TRS4 = Audio Jack (TRS) 3.5mm [package="PG203J [THT]"]
  TRS5 = Audio Jack (TRS) 3.5mm [package="PG203J [THT]"]
  TRS6 = Audio Jack (TRS) 3.5mm [package="PG203J [THT]"]
  TRS7 = Audio Jack (TRS) 3.5mm [package="PG203J [THT]"]
  IC1 = IC, DIP package, 16 pins [chip_label=MCP3008]
  R1 = Resistor [tolerance=±5% resistance=1M package=THT]
  R2 = Resistor [tolerance=±5% resistance=1M package=THT]
  R3 = Resistor [tolerance=±5% resistance=1M package=THT]
  R4 = Resistor [tolerance=±5% resistance=1M package=THT]
  R5 = Resistor [tolerance=±5% resistance=1M package=THT]
  R6 = Resistor [tolerance=±5% resistance=1M package=THT]
  R7 = Resistor [tolerance=±5% resistance=1M package=THT]
  D2 = Rectifier Diode
  D3 = Rectifier Diode
  D4 = Rectifier Diode
  D5 = Rectifier Diode
  D6 = Rectifier Diode
  D7 = Rectifier Diode
  Raspberry_Pi_1 = Raspberry Pi 3 [part_number=RPI-3-V1.2]
  TRS8 = Audio Jack (TRS) 3.5mm [package="PG203J [THT]"]
  D8 = Rectifier Diode
  R8 = Resistor [tolerance=±5% resistance=1M package=THT]

nets:
  N1: TRS1.Ring, D1.anode, TRS2.Ring, TRS3.Ring, TRS4.Ring, TRS5.Ring, TRS6.Ring, TRS7.Ring, IC1.pin9, IC1.pin14, R1.Pin_1, R2.Pin_1, R3.Pin_1, R4.Pin_1, R5.Pin_1, R6.Pin_1, R7.Pin_1, D2.anode, D3.anode, D4.anode, D5.anode, D6.anode, D7.anode, Raspberry_Pi_1.GND, TRS8.Ring, D8.anode, R8.Pin_1
  N2: TRS1.Tip, D1.cathode, IC1.pin1, R1.Pin_0
  N3: TRS2.Tip, IC1.pin2, R2.Pin_0, D2.cathode
  N4: TRS3.Tip, IC1.pin3, R3.Pin_0, D3.cathode
  N5: TRS4.Tip, IC1.pin4, R4.Pin_0, D4.cathode
  N6: TRS5.Tip, IC1.pin5, R5.Pin_0, D5.cathode
  N7: TRS6.Tip, IC1.pin6, R6.Pin_0, D6.cathode
  N8: TRS7.Tip, IC1.pin7, R7.Pin_0, D7.cathode
  N9: IC1.pin8, TRS8.Tip, D8.cathode, R8.Pin_0
  N10: IC1.pin10, Raspberry_Pi_1.GIPO8
  N11: IC1.pin11, Raspberry_Pi_1.GIPO10
  N12: IC1.pin12, Raspberry_Pi_1.GIPO9
  N13: IC1.pin13, Raspberry_Pi_1.GIPO11
  N14: IC1.pin15, IC1.pin16, Raspberry_Pi_1.5V

custom parts:
  Rectifier Diode: Ageneral purpose zener diode
